// Logisim project Processor.circ as structural Verilog: 6 circuits, main circuit main
module main (
);

  wire ALUSrc, and_1_out, and_2_out, beq, bne, CLK, jal, jr, Jump, MemRead, MemtoReg, MemWrite, or_1_out,
       or_2_out, RegDst, RegWrite, Zero;
  wire [2:0] ALUOp, multiplexer_4_out, multiplexer_5_out, rom_1_data, rom_1_data_2, rom_1_data_3,
       rom_1_data_4;
  wire [3:0] rom_1_data_5;
  wire [7:0] PC_q_2;
  wire [13:0] PC_q;
  wire [15:0] adder_2_out, alu_1_result, bit_extender_1_out, jr_reg, multiplexer_1_out, multiplexer_2_out,
       multiplexer_3_out, multiplexer_6_out, multiplexer_7_out, multiplexer_8_out, PC_plus4, ram_1_dout,
       register_file_1_read_data_2, shifter_1_out;
  wire [15:14] PC_q_3;

  Multiplexer #(.width(16)) multiplexer_1 (.in0(multiplexer_2_out), .in1(jr_reg), .out(multiplexer_1_out), .sel(jr));
  Clock clock_1 (.out(CLK));
  Register #(.width(16)) PC (
    .D(multiplexer_1_out), .clk(CLK), .Q({PC_q_3, PC_q[13:10], PC_q_2, PC_q[1:0]}));  // open: en, clr
  Multiplexer #(.width(16)) multiplexer_2 (
    .in0(multiplexer_3_out), .in1({PC_q_3, rom_1_data_4, rom_1_data_3, rom_1_data_2, rom_1_data, 2'b00}),
    .out(multiplexer_2_out), .sel(or_1_out));
  or or_1 (or_1_out, Jump, jal);
  ROM #(.dataWidth(16), .misaligned("true")) rom_1 (
    .addr(PC_q_2), .data({rom_1_data_5, rom_1_data_4, rom_1_data_3, rom_1_data_2, rom_1_data}));
  Adder #(.width(16)) adder_1 (
    .a({PC_q_3, PC_q[13:10], PC_q_2, PC_q[1:0]}), .b(16'h4), .out(PC_plus4));  // open: cin, cout
  Shifter #(.width(16)) shifter_1 (.in(bit_extender_1_out), .\dist (4'b0010), .out(shifter_1_out));
  Multiplexer #(.width(16)) multiplexer_3 (.in0(PC_plus4), .in1(adder_2_out), .out(multiplexer_3_out), .sel(or_2_out));
  or or_2 (or_2_out, and_1_out, and_2_out);
  Adder #(.width(16)) adder_2 (.a(PC_plus4), .b(shifter_1_out), .out(adder_2_out));  // open: cin, cout
  and and_1 (and_1_out, Zero, beq);
  assign bit_extender_1_out = {{10{rom_1_data_2[2]}}, {rom_1_data_2, rom_1_data}};  // Bit_Extender bit_extender_1
  and and_2 (and_2_out, ~Zero, bne);  // AND_Gate
  Multiplexer #(.width(3)) multiplexer_4 (
    .in0(rom_1_data_3), .in1(rom_1_data_2), .out(multiplexer_4_out), .sel(RegDst));
  Register_File register_file_1 (
    .Read_Register_2(rom_1_data_3), .Read_Register_1(rom_1_data_4), .Write_Register(multiplexer_5_out),
    .Write_Data(multiplexer_6_out), .Write_Enable(RegWrite), .Read_Data_2(register_file_1_read_data_2),
    .Read_Data_1(jr_reg));
  Multiplexer #(.width(3)) multiplexer_5 (.in0(multiplexer_4_out), .in1(3'b111), .out(multiplexer_5_out), .sel(jal));
  Multiplexer #(.width(16)) multiplexer_6 (
    .in0(multiplexer_8_out), .in1(PC_plus4), .out(multiplexer_6_out));  // open: sel
  ALU alu_1 (.A(jr_reg), .B(multiplexer_7_out), .Op(ALUOp), .Zero(Zero), .Result(alu_1_result));
  Multiplexer #(.width(16)) multiplexer_7 (
    .in0(register_file_1_read_data_2), .in1(bit_extender_1_out), .out(multiplexer_7_out), .sel(ALUSrc));
  Controller controller_1 (
    .Op(rom_1_data_5), .funct(rom_1_data), .jal(jal), .jr(jr), .MemWrite(MemWrite), .MemtoReg(MemtoReg),
    .MemRead(MemRead), .Branch_Equal(beq), .Branch_Not_Equal(bne), .ALUSrc(ALUSrc), .RegWrite(RegWrite),
    .Jump(Jump), .RegDst(RegDst), .ALUOp(ALUOp));
  RAM #(.addrWidth(16), .asyncread("true"), .dataWidth(16), .\type ("nonvolatile")) ram_1 (
    .addr(alu_1_result), .we(MemWrite), .oe(MemRead), .clk(CLK), .din(register_file_1_read_data_2),
    .dout(ram_1_dout));
  Multiplexer #(.width(16)) multiplexer_8 (
    .in0(alu_1_result), .in1(ram_1_dout), .out(multiplexer_8_out), .sel(MemtoReg));

  // Notes on the sheet:
  //   contents of rom_1 (hex, n*v repeats v):
  //   1040 8005 92 2081 4013 3041 4009 5080 7e00 5db8 2dc0 2c44 527f 8005 1c44 1dc0 5d88 452 7e00
endmodule

module Register_File (
  input  [15:0] Write_Data,
  input  Write_Enable,
  input  [2:0] Write_Register,
  input  [2:0] Read_Register_1,
  input  [2:0] Read_Register_2,
  output [15:0] Read_Data_1,
  output [15:0] Read_Data_2
);

  wire and_1_out, and_2_out, and_3_out, and_4_out, and_5_out, and_6_out, and_7_out, clock_1_out,
       decoder_1_out0, decoder_1_out1, decoder_1_out2, decoder_1_out3, decoder_1_out4, decoder_1_out5,
       decoder_1_out6, decoder_1_out7;
  wire [15:0] register_1_q, register_2_q, register_3_q, register_4_q, register_5_q, register_6_q,
       register_7_q, register_8_q;

  Decoder #(.enable("false"), .select(3)) decoder_1 (
    .out0(decoder_1_out0), .out1(decoder_1_out1), .out2(decoder_1_out2), .out3(decoder_1_out3),
    .out4(decoder_1_out4), .out5(decoder_1_out5), .out6(decoder_1_out6), .out7(decoder_1_out7),
    .sel(Write_Register));
  Clock clock_1 (.out(clock_1_out));
  Register #(.width(16)) register_1 (.D(Write_Data), .Q(register_1_q));  // open: en, clk, clr
  Register #(.width(16)) register_2 (.D(Write_Data), .en(and_1_out), .clk(clock_1_out), .Q(register_2_q));  // open: clr
  and and_1 (and_1_out, Write_Enable, decoder_1_out1);
  Register #(.width(16)) register_3 (.D(Write_Data), .en(and_2_out), .clk(clock_1_out), .Q(register_3_q));  // open: clr
  and and_2 (and_2_out, Write_Enable, decoder_1_out2);
  Register #(.width(16)) register_4 (.D(Write_Data), .en(and_3_out), .clk(clock_1_out), .Q(register_4_q));  // open: clr
  and and_3 (and_3_out, Write_Enable, decoder_1_out3);
  Register #(.width(16)) register_5 (.D(Write_Data), .en(and_4_out), .clk(clock_1_out), .Q(register_5_q));  // open: clr
  and and_4 (and_4_out, Write_Enable, decoder_1_out4);
  Register #(.width(16)) register_6 (.D(Write_Data), .en(and_5_out), .clk(clock_1_out), .Q(register_6_q));  // open: clr
  and and_5 (and_5_out, Write_Enable, decoder_1_out5);
  Register #(.width(16)) register_7 (.D(Write_Data), .en(and_6_out), .clk(clock_1_out), .Q(register_7_q));  // open: clr
  and and_6 (and_6_out, Write_Enable, decoder_1_out6);
  Register #(.width(16)) register_8 (.D(Write_Data), .en(and_7_out), .clk(clock_1_out), .Q(register_8_q));  // open: clr
  and and_7 (and_7_out, Write_Enable, decoder_1_out7);
  Multiplexer #(.select(3), .width(16)) multiplexer_1 (
    .in0(register_1_q), .in1(register_2_q), .in2(register_3_q), .in3(register_4_q), .in4(register_5_q),
    .in5(register_6_q), .in6(register_7_q), .in7(register_8_q), .out(Read_Data_2), .sel(Read_Register_2));
  Multiplexer #(.select(3), .width(16)) multiplexer_2 (
    .in0(register_1_q), .in1(register_2_q), .in2(register_3_q), .in3(register_4_q), .in4(register_5_q),
    .in5(register_6_q), .in6(register_7_q), .in7(register_8_q), .out(Read_Data_1), .sel(Read_Register_1));
endmodule

module ALU_1_bit (
  input  A,
  input  B,
  input  B_Invert,
  input  Cin,
  input  Less,
  input  [1:0] Op,
  output Out1,
  output Cout,
  output Sum
);

  wire and_1_out, multiplexer_1_out, not_1_out, or_1_out;

  Multiplexer multiplexer_1 (.in0(B), .in1(not_1_out), .out(multiplexer_1_out), .sel(B_Invert));
  not not_1 (not_1_out, B);
  and and_1 (and_1_out, A, multiplexer_1_out);
  or or_1 (or_1_out, A, multiplexer_1_out);
  Adder #(.width(1)) adder_1 (.a(A), .b(multiplexer_1_out), .out(Sum), .cin(Cin), .cout(Cout));
  Multiplexer #(.select(2)) multiplexer_2 (
    .in0(and_1_out), .in1(or_1_out), .in2(Sum), .in3(Less), .out(Out1), .sel(Op));
endmodule

module ALU (
  input  [2:0] Op,
  input  [15:0] B,
  input  [15:0] A,
  output [15:0] Result,
  output Zero
);

  wire alu_1_bit_1_cout, alu_1_bit_2_cout, alu_1_bit_3_cout, alu_1_bit_4_cout, alu_1_bit_5_cout,
       alu_1_bit_6_cout, alu_1_bit_7_cout, alu_1_bit_8_cout, alu_1_bit_9_cout, alu_1_bit_10_cout,
       alu_1_bit_11_cout, alu_1_bit_12_cout, alu_1_bit_13_cout, alu_1_bit_14_cout, alu_1_bit_15_cout,
       alu_1_bit_16_sum, or_1_out;

  ALU_1_bit alu_1_bit_1 (
    .A(A[0]), .B(B[0]), .B_Invert(Op[2]), .Cin(Op[2]), .Less(alu_1_bit_16_sum), .Op(Op[1:0]),
    .Cout(alu_1_bit_1_cout), .Out1(Result[0]));  // open: Sum
  ALU_1_bit alu_1_bit_2 (
    .A(A[1]), .B(B[1]), .B_Invert(Op[2]), .Cin(alu_1_bit_1_cout), .Less(1'b0), .Op(Op[1:0]),
    .Cout(alu_1_bit_2_cout), .Out1(Result[1]));  // open: Sum
  ALU_1_bit alu_1_bit_3 (
    .A(A[2]), .B(B[2]), .B_Invert(Op[2]), .Cin(alu_1_bit_2_cout), .Less(1'b0), .Op(Op[1:0]),
    .Cout(alu_1_bit_3_cout), .Out1(Result[2]));  // open: Sum
  ALU_1_bit alu_1_bit_4 (
    .A(A[3]), .B(B[3]), .B_Invert(Op[2]), .Cin(alu_1_bit_3_cout), .Less(1'b0), .Op(Op[1:0]),
    .Cout(alu_1_bit_4_cout), .Out1(Result[3]));  // open: Sum
  ALU_1_bit alu_1_bit_5 (
    .A(A[4]), .B(B[4]), .B_Invert(Op[2]), .Cin(alu_1_bit_4_cout), .Less(1'b0), .Op(Op[1:0]),
    .Cout(alu_1_bit_5_cout), .Out1(Result[4]));  // open: Sum
  ALU_1_bit alu_1_bit_6 (
    .A(A[5]), .B(B[5]), .B_Invert(Op[2]), .Cin(alu_1_bit_5_cout), .Less(1'b0), .Op(Op[1:0]),
    .Cout(alu_1_bit_6_cout), .Out1(Result[5]));  // open: Sum
  ALU_1_bit alu_1_bit_7 (
    .A(A[6]), .B(B[6]), .B_Invert(Op[2]), .Cin(alu_1_bit_6_cout), .Less(1'b0), .Op(Op[1:0]),
    .Cout(alu_1_bit_7_cout), .Out1(Result[6]));  // open: Sum
  ALU_1_bit alu_1_bit_8 (
    .A(A[7]), .B(B[7]), .B_Invert(Op[2]), .Cin(alu_1_bit_7_cout), .Less(1'b0), .Op(Op[1:0]),
    .Cout(alu_1_bit_8_cout), .Out1(Result[7]));  // open: Sum
  ALU_1_bit alu_1_bit_9 (
    .A(A[8]), .B(B[8]), .B_Invert(Op[2]), .Cin(alu_1_bit_8_cout), .Less(1'b0), .Op(Op[1:0]),
    .Cout(alu_1_bit_9_cout), .Out1(Result[8]));  // open: Sum
  ALU_1_bit alu_1_bit_10 (
    .A(A[9]), .B(B[9]), .B_Invert(Op[2]), .Cin(alu_1_bit_9_cout), .Less(1'b0), .Op(Op[1:0]),
    .Cout(alu_1_bit_10_cout), .Out1(Result[9]));  // open: Sum
  ALU_1_bit alu_1_bit_11 (
    .A(A[10]), .B(B[10]), .B_Invert(Op[2]), .Cin(alu_1_bit_10_cout), .Less(1'b0), .Op(Op[1:0]),
    .Cout(alu_1_bit_11_cout), .Out1(Result[10]));  // open: Sum
  ALU_1_bit alu_1_bit_12 (
    .A(A[11]), .B(B[11]), .B_Invert(Op[2]), .Cin(alu_1_bit_11_cout), .Less(1'b0), .Op(Op[1:0]),
    .Cout(alu_1_bit_12_cout), .Out1(Result[11]));  // open: Sum
  ALU_1_bit alu_1_bit_13 (
    .A(A[12]), .B(B[12]), .B_Invert(Op[2]), .Cin(alu_1_bit_12_cout), .Less(1'b0), .Op(Op[1:0]),
    .Cout(alu_1_bit_13_cout), .Out1(Result[12]));  // open: Sum
  ALU_1_bit alu_1_bit_14 (
    .A(A[13]), .B(B[13]), .B_Invert(Op[2]), .Cin(alu_1_bit_13_cout), .Less(1'b0), .Op(Op[1:0]),
    .Cout(alu_1_bit_14_cout), .Out1(Result[13]));  // open: Sum
  ALU_1_bit alu_1_bit_15 (
    .A(A[14]), .B(B[14]), .B_Invert(Op[2]), .Cin(alu_1_bit_14_cout), .Less(1'b0), .Op(Op[1:0]),
    .Cout(alu_1_bit_15_cout), .Out1(Result[14]));  // open: Sum
  ALU_1_bit alu_1_bit_16 (
    .A(A[15]), .B(B[15]), .B_Invert(Op[2]), .Cin(alu_1_bit_15_cout), .Less(1'b0), .Op(Op[1:0]),
    .Sum(alu_1_bit_16_sum), .Out1(Result[15]));  // open: Cout
  or or_1 (or_1_out, Result[0], Result[1], Result[2], Result[3], Result[4], Result[5], Result[6], Result[7], Result[8], Result[9], Result[10], Result[11], Result[12], Result[13], Result[14], Result[15]);
  not not_1 (Zero, or_1_out);
endmodule

module Controller (
  input  [3:0] Op,
  input  [2:0] funct,
  output jal,
  output jr,
  output MemWrite,
  output MemtoReg,
  output MemRead,
  output Branch_Equal,
  output Branch_Not_Equal,
  output ALUSrc,
  output RegWrite,
  output Jump,
  output RegDst,
  output [2:0] ALUOp
);

  wire addi_out, or_1_out;
  wire [2:0] multiplexer_1_out;

  and lw (MemRead, ~Op[3], ~Op[2], ~Op[1], Op[0]);  // AND_Gate
  and beq (Branch_Equal, ~Op[3], ~Op[2], Op[1], Op[0]);  // AND_Gate
  and bne (Branch_Not_Equal, ~Op[3], Op[2], Op[1], ~Op[0]);  // AND_Gate
  and addi (addi_out, ~Op[3], Op[2], ~Op[1], Op[0]);  // AND_Gate
  and Rtype (RegDst, ~Op[3], ~Op[2], ~Op[1], ~Op[0]);  // AND_Gate
  and and_1 (jal, Op[3], ~Op[2], ~Op[1], ~Op[0]);  // AND_Gate
  and and_2 (jr, ~Op[3], Op[2], Op[1], Op[0]);  // AND_Gate
  and sw (MemWrite, ~Op[3], ~Op[2], Op[1], ~Op[0]);  // AND_Gate
  or or_1 (or_1_out, Branch_Not_Equal, Branch_Equal);
  Multiplexer #(.width(3)) multiplexer_1 (.in0(3'b010), .in1(3'b110), .out(multiplexer_1_out), .sel(or_1_out));
  or or_2 (RegWrite, MemRead, addi_out, jal, RegDst);
  and and_3 (Jump, ~Op[3], Op[2], ~Op[1], ~Op[0]);  // AND_Gate
  or or_3 (ALUSrc, MemWrite, MemRead, addi_out);
  Multiplexer #(.width(3)) multiplexer_2 (.in0(multiplexer_1_out), .in1(funct), .out(ALUOp), .sel(RegDst));

  assign MemtoReg = MemRead;
endmodule

module Task1 (
  output [15:0] out_1
);

  wire clock_1_out;
  wire [15:0] adder_1_out, register_1_q;

  Register #(.width(16)) register_1 (.D(adder_1_out), .clk(clock_1_out), .Q(register_1_q));  // open: en, clr
  Clock clock_1 (.out(clock_1_out));
  Adder #(.width(16)) adder_1 (.a(register_1_q), .b(16'h1), .out(adder_1_out));  // open: cin, cout
  ROM #(.dataWidth(16)) rom_1 (.addr(register_1_q[7:0]), .data(out_1));

  // Notes on the sheet:
  //   contents of rom_1 (hex, n*v repeats v):
  //   0 1 2 3 4 5 6 7 8 9 a b c d e f 10 11 12 13 14 15 16 17 18 19 1a 1b 1c 1d 1e 1f 20 21 22 23 24 25 26
  //   27 28 29 2a 2b 2c 2d 2e 2f 30 31 32 33 34 35 36 37 38 39 3a 3b 3c 3d 3e 3f 40 41 42 43 44 45 46 47
  //   48 49 4a 4b 4c 4d 4e 4f 50 51 52 53 54 55 56 57 58 59 5a 5b 5c 5d 5e 5f 60 61 62 63
endmodule
