// Logisim project Assignment10.circ as structural Verilog: 2 circuits, main circuit main
module main (
);

  Controller controller_1 ();  // open: Opcode, RegDst, Branch, MemRead, FunctionCode, MemtoReg_2, ALUOp, MemWrite, ALUSrc, RegWrite
endmodule

module Controller (
  input  [3:0] Opcode,
  input  RegDst,
  input  Branch,
  input  MemRead,
  input  [2:0] FunctionCode,
  input  MemtoReg_2,
  input  [2:0] ALUOp,
  input  MemWrite,
  input  ALUSrc,
  input  RegWrite
);

  wire and_6_out;
  wire [2:0] multiplexer_1_out, multiplexer_2_out, not_1_out, not_2_out, not_3_out;

  and and_1 (Branch, Opcode[3], Opcode[2], ~Opcode[0]);  // AND_Gate
  and and_2 (MemRead, Opcode[3], Opcode[2], Opcode[1], Opcode[0]);
  and and_3 (MemtoReg_2, Opcode[3], Opcode[1]);
  and and_4 (MemWrite, ~Opcode[3], ~Opcode[2], Opcode[1], ~Opcode[0]);  // AND_Gate
  and and_5 (ALUSrc, Opcode[3], Opcode[1]);  // AND_Gate
  and and_6 (and_6_out, ~Opcode[2], ~Opcode[0]);  // AND_Gate
  assign not_1_out = ~FunctionCode;  // NOT_Gate not_1, 3 bits wide
  Multiplexer #(.width(3)) multiplexer_1 (
    .in0(FunctionCode), .in1(not_1_out), .out(multiplexer_1_out), .sel(Opcode[0]));
  or or_1 (RegWrite, Opcode[3], and_6_out, Opcode[1]);
  assign not_2_out = ~FunctionCode;  // NOT_Gate not_2, 3 bits wide
  Multiplexer #(.width(3)) multiplexer_2 (
    .in0(multiplexer_1_out), .in1(not_2_out), .out(multiplexer_2_out), .sel(Opcode[1]));
  assign not_3_out = ~FunctionCode;  // NOT_Gate not_3, 3 bits wide
  Multiplexer #(.width(3)) multiplexer_3 (.in0(multiplexer_2_out), .in1(not_3_out), .out(ALUOp), .sel(Opcode[2]));

  assign RegDst = Opcode[3];
endmodule
