// Logisim project Assignment11.circ as structural Verilog: 4 circuits, main circuit main11
module main11 (
);

  wire alu_1_zero, beq_out, bne_out, clock_1_out, clock_2_out, controller11_1_alusrc,
       controller11_1_branchequal, controller11_1_jump, controller11_1_jumpal, controller11_1_jumpr,
       controller11_1_memread, controller11_1_memtoreg, controller11_1_memwrite, controller11_1_neqbranch,
       controller11_1_regdest, controller11_1_regwrite, or_1_out;
  wire [2:0] controller11_1_aluop, multiplexer_1_out, multiplexer_2_out, rom_1_data_2, rom_1_data_3;
  wire [3:0] rom_1_data_4;
  wire [5:0] rom_1_data;
  wire [11:0] PC_q;
  wire [15:0] adder_2_out, alu_1_result, bit_extender_1_out, multiplexer_3_out, multiplexer_4_out,
       multiplexer_5_out, multiplexer_6_out, multiplexer_7_out, multiplexer_8_out, PC_q_2, PCplus4,
       ram_1_dout, register_file_1_read_data_1, register_file_1_read_data_2, shifter_1_out, shifter_2_out;

  Register #(.width(16)) PC (
    .D(multiplexer_7_out), .clk(clock_1_out), .Q({PC_q_2[15:14], PC_q, PC_q_2[1:0]}));  // open: en, clr
  Clock clock_1 (.out(clock_1_out));
  ROM #(.dataWidth(16)) rom_1 (.addr(PC_q[7:0]), .data({rom_1_data_4, rom_1_data_3, rom_1_data_2, rom_1_data}));
  Adder #(.width(16)) adder_1 (.a({PC_q_2[15:14], PC_q, PC_q_2[1:0]}), .b(16'h4), .out(PCplus4));  // open: cin, cout
  Shifter #(.width(16)) shifter_1 (
    .in({rom_1_data_4, rom_1_data_3, rom_1_data_2, rom_1_data}), .\dist (4'b0010), .out(shifter_1_out));
  Multiplexer #(.width(3)) multiplexer_1 (
    .in0(rom_1_data_2), .in1(rom_1_data[5:3]), .out(multiplexer_1_out), .sel(controller11_1_regdest));
  assign bit_extender_1_out = {{10{rom_1_data[5]}}, rom_1_data};  // Bit_Extender bit_extender_1
  Controller11 controller11_1 (
    .FunctionCode(rom_1_data[2:0]), .OPcode(rom_1_data_4), .neqbranch(controller11_1_neqbranch),
    .MemRead(controller11_1_memread), .MemtoReg(controller11_1_memtoreg), .MemWrite(controller11_1_memwrite),
    .ALUOp(controller11_1_aluop), .ALUSrc(controller11_1_alusrc), .RegWrite(controller11_1_regwrite),
    .Jump(controller11_1_jump), .jumpR(controller11_1_jumpr), .JumpAL(controller11_1_jumpal),
    .RegDest(controller11_1_regdest), .branchequal(controller11_1_branchequal));
  Register_File register_file_1 (
    .Read_Register_2(rom_1_data_2), .Read_Register_1(rom_1_data_3), .Write_Register(multiplexer_2_out),
    .Write_Data(multiplexer_3_out), .Write_Enable(controller11_1_regwrite),
    .Read_Data_2(register_file_1_read_data_2), .Read_Data_1(register_file_1_read_data_1));
  Multiplexer #(.width(3)) multiplexer_2 (
    .in0(multiplexer_1_out), .in1(3'b111), .out(multiplexer_2_out), .sel(controller11_1_jumpal));
  Multiplexer #(.width(16)) multiplexer_3 (
    .in0(multiplexer_8_out), .in1(PCplus4), .out(multiplexer_3_out), .sel(controller11_1_jumpal));
  Shifter #(.width(16)) shifter_2 (.in(bit_extender_1_out), .\dist (4'b0010), .out(shifter_2_out));
  Multiplexer #(.width(16)) multiplexer_4 (
    .in0(register_file_1_read_data_2), .in1(bit_extender_1_out), .out(multiplexer_4_out),
    .sel(controller11_1_alusrc));
  Adder #(.width(16)) adder_2 (.a(PCplus4), .b(shifter_2_out), .out(adder_2_out));  // open: cin, cout
  ALU alu_1 (
    .A(register_file_1_read_data_1), .B(multiplexer_4_out), .Op(controller11_1_aluop), .Zero(alu_1_zero),
    .Result(alu_1_result));
  Multiplexer #(.width(16)) multiplexer_5 (.in0(PCplus4), .in1(adder_2_out), .out(multiplexer_5_out), .sel(or_1_out));
  or or_1 (or_1_out, bne_out, beq_out);
  Clock clock_2 (.out(clock_2_out));
  Multiplexer #(.width(16)) multiplexer_6 (
    .in0(multiplexer_5_out), .in1({PC_q_2[15:14], shifter_1_out[13:2], PC_q_2[1:0]}),
    .out(multiplexer_6_out), .sel(controller11_1_jump));
  and beq (beq_out, controller11_1_branchequal, alu_1_zero);
  RAM #(.addrWidth(16), .asyncread("true"), .dataWidth(16)) ram_1 (
    .addr(alu_1_result), .we(controller11_1_memwrite), .oe(controller11_1_memread), .clk(clock_2_out),
    .din(register_file_1_read_data_2), .dout(ram_1_dout));
  Multiplexer #(.width(16)) multiplexer_7 (
    .in0(multiplexer_6_out), .in1(register_file_1_read_data_1), .out(multiplexer_7_out),
    .sel(controller11_1_jumpr));
  and bne (bne_out, controller11_1_neqbranch, ~alu_1_zero);  // AND_Gate
  Multiplexer #(.width(16)) multiplexer_8 (
    .in0(alu_1_result), .in1(ram_1_dout), .out(multiplexer_8_out), .sel(controller11_1_memtoreg));

  // Notes on the sheet:
  //   contents of rom_1 (hex, n*v repeats v):
  //   1040 1081 51a8 8006 20c2 4012 5101 6882 5a 7e00 5dbf 2dc0 54bf 8006 65a 1dc0 5d81 7e00
  //   multiplexter for jal: you have to change what you write to the write data
  //   stores the adress in the register file to go back to later
endmodule

module ALU_1_bit11 (
  input  A,
  input  B,
  input  B_Invert,
  input  Cin,
  input  Less,
  input  [1:0] Op,
  output Out1,
  output Cout,
  output Sum
);

  wire and_1_out, multiplexer_1_out, not_1_out, or_1_out;

  Multiplexer multiplexer_1 (.in0(B), .in1(not_1_out), .out(multiplexer_1_out), .sel(B_Invert));
  not not_1 (not_1_out, B);
  and and_1 (and_1_out, A, multiplexer_1_out);
  or or_1 (or_1_out, A, multiplexer_1_out);
  Adder #(.width(1)) adder_1 (.a(A), .b(multiplexer_1_out), .out(Sum), .cin(Cin), .cout(Cout));
  Multiplexer #(.select(2)) multiplexer_2 (
    .in0(and_1_out), .in1(or_1_out), .in2(Sum), .in3(Less), .out(Out1), .sel(Op));
endmodule

module ALU11 (
  input  [2:0] Op,
  input  [15:0] B,
  input  [15:0] A,
  output [15:0] Result,
  output Zero
);

  wire alu_1_bit11_1_cout, alu_1_bit11_2_cout, alu_1_bit11_3_cout, alu_1_bit11_4_cout, alu_1_bit11_5_cout,
       alu_1_bit11_6_cout, alu_1_bit11_7_cout, alu_1_bit11_8_cout, alu_1_bit11_9_cout, alu_1_bit11_10_cout,
       alu_1_bit11_11_cout, alu_1_bit11_12_cout, alu_1_bit11_13_cout, alu_1_bit11_14_cout,
       alu_1_bit11_15_cout, alu_1_bit11_16_sum, or_1_out;

  ALU_1_bit11 alu_1_bit11_1 (
    .A(A[0]), .B(B[0]), .B_Invert(Op[2]), .Cin(Op[2]), .Less(alu_1_bit11_16_sum), .Op(Op[1:0]),
    .Cout(alu_1_bit11_1_cout), .Out1(Result[0]));  // open: Sum
  ALU_1_bit11 alu_1_bit11_2 (
    .A(A[1]), .B(B[1]), .B_Invert(Op[2]), .Cin(alu_1_bit11_1_cout), .Less(1'b0), .Op(Op[1:0]),
    .Cout(alu_1_bit11_2_cout), .Out1(Result[1]));  // open: Sum
  ALU_1_bit11 alu_1_bit11_3 (
    .A(A[2]), .B(B[2]), .B_Invert(Op[2]), .Cin(alu_1_bit11_2_cout), .Less(1'b0), .Op(Op[1:0]),
    .Cout(alu_1_bit11_3_cout), .Out1(Result[2]));  // open: Sum
  ALU_1_bit11 alu_1_bit11_4 (
    .A(A[3]), .B(B[3]), .B_Invert(Op[2]), .Cin(alu_1_bit11_3_cout), .Less(1'b0), .Op(Op[1:0]),
    .Cout(alu_1_bit11_4_cout), .Out1(Result[3]));  // open: Sum
  ALU_1_bit11 alu_1_bit11_5 (
    .A(A[4]), .B(B[4]), .B_Invert(Op[2]), .Cin(alu_1_bit11_4_cout), .Less(1'b0), .Op(Op[1:0]),
    .Cout(alu_1_bit11_5_cout), .Out1(Result[4]));  // open: Sum
  ALU_1_bit11 alu_1_bit11_6 (
    .A(A[5]), .B(B[5]), .B_Invert(Op[2]), .Cin(alu_1_bit11_5_cout), .Less(1'b0), .Op(Op[1:0]),
    .Cout(alu_1_bit11_6_cout), .Out1(Result[5]));  // open: Sum
  ALU_1_bit11 alu_1_bit11_7 (
    .A(A[6]), .B(B[6]), .B_Invert(Op[2]), .Cin(alu_1_bit11_6_cout), .Less(1'b0), .Op(Op[1:0]),
    .Cout(alu_1_bit11_7_cout), .Out1(Result[6]));  // open: Sum
  ALU_1_bit11 alu_1_bit11_8 (
    .A(A[7]), .B(B[7]), .B_Invert(Op[2]), .Cin(alu_1_bit11_7_cout), .Less(1'b0), .Op(Op[1:0]),
    .Cout(alu_1_bit11_8_cout), .Out1(Result[7]));  // open: Sum
  ALU_1_bit11 alu_1_bit11_9 (
    .A(A[8]), .B(B[8]), .B_Invert(Op[2]), .Cin(alu_1_bit11_8_cout), .Less(1'b0), .Op(Op[1:0]),
    .Cout(alu_1_bit11_9_cout), .Out1(Result[8]));  // open: Sum
  ALU_1_bit11 alu_1_bit11_10 (
    .A(A[9]), .B(B[9]), .B_Invert(Op[2]), .Cin(alu_1_bit11_9_cout), .Less(1'b0), .Op(Op[1:0]),
    .Cout(alu_1_bit11_10_cout), .Out1(Result[9]));  // open: Sum
  ALU_1_bit11 alu_1_bit11_11 (
    .A(A[10]), .B(B[10]), .B_Invert(Op[2]), .Cin(alu_1_bit11_10_cout), .Less(1'b0), .Op(Op[1:0]),
    .Cout(alu_1_bit11_11_cout), .Out1(Result[10]));  // open: Sum
  ALU_1_bit11 alu_1_bit11_12 (
    .A(A[11]), .B(B[11]), .B_Invert(Op[2]), .Cin(alu_1_bit11_11_cout), .Less(1'b0), .Op(Op[1:0]),
    .Cout(alu_1_bit11_12_cout), .Out1(Result[11]));  // open: Sum
  ALU_1_bit11 alu_1_bit11_13 (
    .A(A[12]), .B(B[12]), .B_Invert(Op[2]), .Cin(alu_1_bit11_12_cout), .Less(1'b0), .Op(Op[1:0]),
    .Cout(alu_1_bit11_13_cout), .Out1(Result[12]));  // open: Sum
  ALU_1_bit11 alu_1_bit11_14 (
    .A(A[13]), .B(B[13]), .B_Invert(Op[2]), .Cin(alu_1_bit11_13_cout), .Less(1'b0), .Op(Op[1:0]),
    .Cout(alu_1_bit11_14_cout), .Out1(Result[13]));  // open: Sum
  ALU_1_bit11 alu_1_bit11_15 (
    .A(A[14]), .B(B[14]), .B_Invert(Op[2]), .Cin(alu_1_bit11_14_cout), .Less(1'b0), .Op(Op[1:0]),
    .Cout(alu_1_bit11_15_cout), .Out1(Result[14]));  // open: Sum
  ALU_1_bit11 alu_1_bit11_16 (
    .A(A[15]), .B(B[15]), .B_Invert(Op[2]), .Cin(alu_1_bit11_15_cout), .Less(1'b0), .Op(Op[1:0]),
    .Sum(alu_1_bit11_16_sum), .Out1(Result[15]));  // open: Cout
  or or_1 (or_1_out, Result[0], Result[1], Result[2], Result[3], Result[4], Result[5], Result[6], Result[7], Result[8], Result[9], Result[10], Result[11], Result[12], Result[13], Result[14], Result[15]);
  not not_1 (Zero, or_1_out);
endmodule

module Controller11 (
  input  [2:0] FunctionCode,
  input  [3:0] OPcode,
  output [2:0] ALUOp,
  output neqbranch,
  output branchequal,
  output MemtoReg,
  output ALUSrc,
  output Jump,
  output jumpR,
  output JumpAL,
  output RegDest,
  output MemRead,
  output MemWrite,
  output RegWrite
);

  wire addi_out, j_out, or_1_out;
  wire [2:0] multiplexer_1_out;

  and SW (MemWrite, ~OPcode[3], ~OPcode[2], OPcode[1], ~OPcode[0]);  // AND_Gate
  and addi (addi_out, ~OPcode[3], OPcode[2], ~OPcode[1], OPcode[0]);  // AND_Gate
  and R (RegDest, ~OPcode[3], ~OPcode[2], ~OPcode[1], ~OPcode[0]);  // AND_Gate
  and LW (MemRead, ~OPcode[3], ~OPcode[2], ~OPcode[1], OPcode[0]);  // AND_Gate
  and beq (branchequal, ~OPcode[3], ~OPcode[2], OPcode[1], OPcode[0]);  // AND_Gate
  and bne (neqbranch, ~OPcode[3], OPcode[2], OPcode[1], ~OPcode[0]);  // AND_Gate
  and jr (jumpR, ~OPcode[3], OPcode[2], OPcode[1], OPcode[0]);  // AND_Gate
  and j (j_out, ~OPcode[3], OPcode[2], ~OPcode[1], ~OPcode[0]);  // AND_Gate
  and jal (JumpAL, OPcode[3], ~OPcode[2], ~OPcode[1], ~OPcode[0]);  // AND_Gate
  or or_1 (or_1_out, branchequal, neqbranch);
  Multiplexer #(.width(3)) multiplexer_1 (.in0(3'b010), .in1(3'b110), .out(multiplexer_1_out), .sel(or_1_out));
  Multiplexer #(.width(3)) multiplexer_2 (.in0(multiplexer_1_out), .in1(FunctionCode), .out(ALUOp), .sel(RegDest));
  or or_2 (ALUSrc, MemRead, MemWrite, addi_out);
  or or_3 (RegWrite, RegDest, JumpAL, MemRead, addi_out);
  or or_4 (Jump, j_out, JumpAL);

  assign MemtoReg = MemRead;

  // Notes on the sheet:
  //   branch if beq and if zero == true
  //   branch if bne and !zero
endmodule
