// Logisim project Assignment11.circ as structural Verilog: 5 circuits, main circuit main
module main (
);

  wire and_1_out, clock_1_out, clock_2_out, undriven, undriven_2, undriven_3, undriven_4, undriven_5,
       undriven_7, undriven_8;
  wire [2:0] multiplexer_1_out;
  wire [15:0] adder_1_out, adder_2_out, bit_extender_1_out, multiplexer_2_out, multiplexer_3_out,
       multiplexer_4_out, PC_q, ram_1_dout, rom_1_data, shifter_1_out, undriven_6, undriven_9;

  Register #(.width(16)) PC (.D(multiplexer_3_out), .clk(clock_1_out), .Q(PC_q));  // open: en, clr
  Clock clock_1 (.out(clock_1_out));
  Adder #(.width(16)) adder_1 (.a(PC_q), .b(16'h4), .out(adder_1_out));  // open: cin, cout
  ROM #(.dataWidth(16)) rom_1 (.addr(PC_q[9:2]), .data(rom_1_data));
  Multiplexer #(.width(3)) multiplexer_1 (
    .in0(rom_1_data[8:6]), .in1(rom_1_data[5:3]), .out(multiplexer_1_out), .sel(undriven));
  assign bit_extender_1_out = {{10{rom_1_data[5]}}, rom_1_data[5:0]};  // Bit_Extender bit_extender_1
  Adder #(.width(16)) adder_2 (.a(adder_1_out), .b(shifter_1_out), .out(adder_2_out));  // open: cin, cout
  Shifter #(.width(16)) shifter_1 (.in(bit_extender_1_out), .\dist (4'b0010), .out(shifter_1_out));
  Multiplexer #(.width(16)) multiplexer_2 (
    .in0(undriven_6), .in1(bit_extender_1_out), .out(multiplexer_2_out), .sel(undriven_5));
  Multiplexer #(.width(16)) multiplexer_3 (
    .in0(adder_1_out), .in1(adder_2_out), .out(multiplexer_3_out), .sel(and_1_out));
  and and_1 (and_1_out, undriven_7, undriven_8);
  RAM #(.addrWidth(16), .asyncread("true"), .dataWidth(16)) ram_1 (
    .addr(undriven_9), .we(undriven_4), .oe(undriven_2), .clk(clock_2_out), .din(undriven_6),
    .dout(ram_1_dout));
  Clock clock_2 (.out(clock_2_out));
  Multiplexer #(.width(16)) multiplexer_4 (
    .in0(undriven_9), .in1(ram_1_dout), .out(multiplexer_4_out), .sel(undriven_3));

  // Notes on the sheet:
  //   contents of rom_1 (hex, n*v repeats v):
  //   5040 5080 50c0 22c0 5101 5154 3547 5241 2300 8f2 58c0 5d00 5481 3e38
endmodule

module Controller (
  input  [2:0] FunctionCode,
  input  [3:0] OPcode,
  output [2:0] ALUOp,
  output Branch,
  output MemtoReg,
  output ALUSrc,
  output Jump,
  output RegDest,
  output MemRead,
  output MemWrite,
  output RegWrite
);

  wire addi_out, beq_out, bne_out;
  wire [2:0] multiplexer_1_out;

  and SW (MemWrite, ~OPcode[3], ~OPcode[2], OPcode[1], ~OPcode[0]);  // AND_Gate
  and addi (addi_out, ~OPcode[3], OPcode[2], ~OPcode[1], OPcode[0]);  // AND_Gate
  and R (RegDest, ~OPcode[3], ~OPcode[2], ~OPcode[1], ~OPcode[0]);  // AND_Gate
  and LW (MemRead, ~OPcode[3], ~OPcode[2], ~OPcode[1], OPcode[0]);  // AND_Gate
  and beq (beq_out, ~OPcode[3], ~OPcode[2], OPcode[1], OPcode[0]);  // AND_Gate
  and bne (bne_out, ~OPcode[3], OPcode[2], OPcode[1], ~OPcode[0]);  // AND_Gate
  // AND_Gate jr has open pins: in0=OPcode[3], in1=OPcode[2], in2=OPcode[1], in3=OPcode[0], out=open
  and j (Jump, ~OPcode[3], OPcode[2], ~OPcode[1], ~OPcode[0]);  // AND_Gate
  // AND_Gate jal has open pins: in0=OPcode[3], in1=OPcode[2], in2=OPcode[1], in3=OPcode[0], out=open
  or or_1 (Branch, beq_out, bne_out);
  Multiplexer #(.width(3)) multiplexer_1 (.in0(3'b010), .in1(3'b110), .out(multiplexer_1_out), .sel(beq_out));
  Multiplexer #(.width(3)) multiplexer_2 (.in0(multiplexer_1_out), .in1(FunctionCode), .out(ALUOp), .sel(RegDest));
  or or_2 (ALUSrc, MemRead, MemWrite, addi_out);
  or or_3 (RegWrite, RegDest, MemRead, addi_out);

  assign MemtoReg = MemRead;
endmodule

module ALU_1_bit (
  input  A,
  input  B,
  input  B_Invert,
  input  Cin,
  input  Less,
  input  [1:0] Op,
  output Out1,
  output Cout,
  output Sum
);

  wire and_1_out, multiplexer_1_out, not_1_out, or_1_out;

  Multiplexer multiplexer_1 (.in0(B), .in1(not_1_out), .out(multiplexer_1_out), .sel(B_Invert));
  not not_1 (not_1_out, B);
  and and_1 (and_1_out, A, multiplexer_1_out);
  or or_1 (or_1_out, A, multiplexer_1_out);
  Adder #(.width(1)) adder_1 (.a(A), .b(multiplexer_1_out), .out(Sum), .cin(Cin), .cout(Cout));
  Multiplexer #(.select(2)) multiplexer_2 (
    .in0(and_1_out), .in1(or_1_out), .in2(Sum), .in3(Less), .out(Out1), .sel(Op));
endmodule

module ALU (
  input  [2:0] Op,
  input  [15:0] B,
  input  [15:0] A,
  output [15:0] Result,
  output Zero
);

  wire or_1_out;

  or or_1 (or_1_out, Result[0], Result[1], Result[2], Result[3], Result[4], Result[5], Result[6], Result[7], Result[8], Result[9], Result[10], Result[11], Result[12], Result[13], Result[14], Result[15]);
  not not_1 (Zero, or_1_out);
endmodule

module Register_File (
  input  [15:0] Write_Data,
  input  Write_Enable,
  input  [2:0] Write_Register,
  input  [2:0] Read_Register_1,
  input  [2:0] Read_Register_2,
  output [15:0] Read_Data_1,
  output [15:0] Read_Data_2
);

  wire and_1_out, and_2_out, and_3_out, and_4_out, and_5_out, and_6_out, and_7_out, clock_1_out,
       decoder_1_out0, decoder_1_out1, decoder_1_out2, decoder_1_out3, decoder_1_out4, decoder_1_out5,
       decoder_1_out6, decoder_1_out7;
  wire [15:0] register_1_q, register_2_q, register_3_q, register_4_q, register_5_q, register_6_q,
       register_7_q, register_8_q;

  Decoder #(.enable("false"), .select(3)) decoder_1 (
    .out0(decoder_1_out0), .out1(decoder_1_out1), .out2(decoder_1_out2), .out3(decoder_1_out3),
    .out4(decoder_1_out4), .out5(decoder_1_out5), .out6(decoder_1_out6), .out7(decoder_1_out7),
    .sel(Write_Register));
  Clock clock_1 (.out(clock_1_out));
  Register #(.width(16)) register_1 (.D(Write_Data), .Q(register_1_q));  // open: en, clk, clr
  Register #(.width(16)) register_2 (.D(Write_Data), .en(and_1_out), .clk(clock_1_out), .Q(register_2_q));  // open: clr
  and and_1 (and_1_out, Write_Enable, decoder_1_out1);
  Register #(.width(16)) register_3 (.D(Write_Data), .en(and_2_out), .clk(clock_1_out), .Q(register_3_q));  // open: clr
  and and_2 (and_2_out, Write_Enable, decoder_1_out2);
  Register #(.width(16)) register_4 (.D(Write_Data), .en(and_3_out), .clk(clock_1_out), .Q(register_4_q));  // open: clr
  and and_3 (and_3_out, Write_Enable, decoder_1_out3);
  Register #(.width(16)) register_5 (.D(Write_Data), .en(and_4_out), .clk(clock_1_out), .Q(register_5_q));  // open: clr
  and and_4 (and_4_out, Write_Enable, decoder_1_out4);
  Register #(.width(16)) register_6 (.D(Write_Data), .en(and_5_out), .clk(clock_1_out), .Q(register_6_q));  // open: clr
  and and_5 (and_5_out, Write_Enable, decoder_1_out5);
  Register #(.width(16)) register_7 (.D(Write_Data), .en(and_6_out), .clk(clock_1_out), .Q(register_7_q));  // open: clr
  and and_6 (and_6_out, Write_Enable, decoder_1_out6);
  Register #(.width(16)) register_8 (.D(Write_Data), .en(and_7_out), .clk(clock_1_out), .Q(register_8_q));  // open: clr
  and and_7 (and_7_out, Write_Enable, decoder_1_out7);
  Multiplexer #(.select(3), .width(16)) multiplexer_1 (
    .in0(register_1_q), .in1(register_2_q), .in2(register_3_q), .in3(register_4_q), .in4(register_5_q),
    .in5(register_6_q), .in6(register_7_q), .in7(register_8_q), .out(Read_Data_2), .sel(Read_Register_2));
  Multiplexer #(.select(3), .width(16)) multiplexer_2 (
    .in0(register_1_q), .in1(register_2_q), .in2(register_3_q), .in3(register_4_q), .in4(register_5_q),
    .in5(register_6_q), .in6(register_7_q), .in7(register_8_q), .out(Read_Data_1), .sel(Read_Register_1));
endmodule
