// Logisim project Assignment9-1.circ as structural Verilog: 3 circuits, main circuit Register_File
module Register_File (
  input  [15:0] Write_Data,
  input  Write_Enable,
  input  [2:0] Write_Register,
  input  [2:0] Read_Register_1,
  input  [2:0] Read_Register_2,
  output [15:0] Read_Data_1,
  output [15:0] Read_Data_2
);

  wire and_1_out, and_2_out, and_3_out, and_4_out, and_5_out, and_6_out, and_7_out, clock_1_out,
       decoder_1_out0, decoder_1_out1, decoder_1_out2, decoder_1_out3, decoder_1_out4, decoder_1_out5,
       decoder_1_out6, decoder_1_out7;
  wire [15:0] register_1_q, register_2_q, register_3_q, register_4_q, register_5_q, register_6_q,
       register_7_q, register_8_q;

  Decoder #(.enable("false"), .select(3)) decoder_1 (
    .out0(decoder_1_out0), .out1(decoder_1_out1), .out2(decoder_1_out2), .out3(decoder_1_out3),
    .out4(decoder_1_out4), .out5(decoder_1_out5), .out6(decoder_1_out6), .out7(decoder_1_out7),
    .sel(Write_Register));
  Clock clock_1 (.out(clock_1_out));
  Register #(.width(16)) register_1 (.D(Write_Data), .Q(register_1_q));  // open: en, clk, clr
  Register #(.width(16)) register_2 (.D(Write_Data), .en(and_1_out), .clk(clock_1_out), .Q(register_2_q));  // open: clr
  and and_1 (and_1_out, Write_Enable, decoder_1_out1);
  Register #(.width(16)) register_3 (.D(Write_Data), .en(and_2_out), .clk(clock_1_out), .Q(register_3_q));  // open: clr
  and and_2 (and_2_out, Write_Enable, decoder_1_out2);
  Register #(.width(16)) register_4 (.D(Write_Data), .en(and_3_out), .clk(clock_1_out), .Q(register_4_q));  // open: clr
  and and_3 (and_3_out, Write_Enable, decoder_1_out3);
  Register #(.width(16)) register_5 (.D(Write_Data), .en(and_4_out), .clk(clock_1_out), .Q(register_5_q));  // open: clr
  and and_4 (and_4_out, Write_Enable, decoder_1_out4);
  Register #(.width(16)) register_6 (.D(Write_Data), .en(and_5_out), .clk(clock_1_out), .Q(register_6_q));  // open: clr
  and and_5 (and_5_out, Write_Enable, decoder_1_out5);
  Register #(.width(16)) register_7 (.D(Write_Data), .en(and_6_out), .clk(clock_1_out), .Q(register_7_q));  // open: clr
  and and_6 (and_6_out, Write_Enable, decoder_1_out6);
  Register #(.width(16)) register_8 (.D(Write_Data), .en(and_7_out), .clk(clock_1_out), .Q(register_8_q));  // open: clr
  and and_7 (and_7_out, Write_Enable, decoder_1_out7);
  Multiplexer #(.select(3), .width(16)) multiplexer_1 (
    .in0(register_1_q), .in1(register_2_q), .in2(register_3_q), .in3(register_4_q), .in4(register_5_q),
    .in5(register_6_q), .in6(register_7_q), .in7(register_8_q), .out(Read_Data_2), .sel(Read_Register_2));
  Multiplexer #(.select(3), .width(16)) multiplexer_2 (
    .in0(register_1_q), .in1(register_2_q), .in2(register_3_q), .in3(register_4_q), .in4(register_5_q),
    .in5(register_6_q), .in6(register_7_q), .in7(register_8_q), .out(Read_Data_1), .sel(Read_Register_1));
endmodule

module ALU_1_bit (
  input  A,
  input  B,
  input  B_Invert,
  input  Cin,
  input  Less,
  input  [1:0] Op,
  output Out1,
  output Cout,
  output Sum
);

  wire and_1_out, multiplexer_1_out, not_1_out, or_1_out;

  Multiplexer multiplexer_1 (.in0(B), .in1(not_1_out), .out(multiplexer_1_out), .sel(B_Invert));
  not not_1 (not_1_out, B);
  and and_1 (and_1_out, A, multiplexer_1_out);
  or or_1 (or_1_out, A, multiplexer_1_out);
  Adder #(.width(1)) adder_1 (.a(A), .b(multiplexer_1_out), .out(Sum), .cin(Cin), .cout(Cout));
  Multiplexer #(.select(2)) multiplexer_2 (
    .in0(and_1_out), .in1(or_1_out), .in2(Sum), .in3(Less), .out(Out1), .sel(Op));
endmodule

module ALU (
  input  [2:0] Op,
  input  [15:0] B,
  input  [15:0] A,
  output [15:0] Result,
  output Zero
);

  wire alu_1_bit_1_cout, alu_1_bit_2_cout, alu_1_bit_3_cout, alu_1_bit_4_cout, alu_1_bit_5_cout,
       alu_1_bit_6_cout, alu_1_bit_7_cout, alu_1_bit_8_cout, alu_1_bit_9_cout, alu_1_bit_10_cout,
       alu_1_bit_11_cout, alu_1_bit_12_cout, alu_1_bit_13_cout, alu_1_bit_14_cout, alu_1_bit_15_cout,
       alu_1_bit_16_sum, or_1_out;

  ALU_1_bit alu_1_bit_1 (
    .A(A[0]), .B(B[0]), .B_Invert(Op[2]), .Cin(Op[2]), .Less(alu_1_bit_16_sum), .Op(Op[1:0]),
    .Cout(alu_1_bit_1_cout), .Out1(Result[0]));  // open: Sum
  ALU_1_bit alu_1_bit_2 (
    .A(A[1]), .B(B[1]), .B_Invert(Op[2]), .Cin(alu_1_bit_1_cout), .Less(1'b0), .Op(Op[1:0]),
    .Cout(alu_1_bit_2_cout), .Out1(Result[1]));  // open: Sum
  ALU_1_bit alu_1_bit_3 (
    .A(A[2]), .B(B[2]), .B_Invert(Op[2]), .Cin(alu_1_bit_2_cout), .Less(1'b0), .Op(Op[1:0]),
    .Cout(alu_1_bit_3_cout), .Out1(Result[2]));  // open: Sum
  ALU_1_bit alu_1_bit_4 (
    .A(A[3]), .B(B[3]), .B_Invert(Op[2]), .Cin(alu_1_bit_3_cout), .Less(1'b0), .Op(Op[1:0]),
    .Cout(alu_1_bit_4_cout), .Out1(Result[3]));  // open: Sum
  ALU_1_bit alu_1_bit_5 (
    .A(A[4]), .B(B[4]), .B_Invert(Op[2]), .Cin(alu_1_bit_4_cout), .Less(1'b0), .Op(Op[1:0]),
    .Cout(alu_1_bit_5_cout), .Out1(Result[4]));  // open: Sum
  ALU_1_bit alu_1_bit_6 (
    .A(A[5]), .B(B[5]), .B_Invert(Op[2]), .Cin(alu_1_bit_5_cout), .Less(1'b0), .Op(Op[1:0]),
    .Cout(alu_1_bit_6_cout), .Out1(Result[5]));  // open: Sum
  ALU_1_bit alu_1_bit_7 (
    .A(A[6]), .B(B[6]), .B_Invert(Op[2]), .Cin(alu_1_bit_6_cout), .Less(1'b0), .Cout(alu_1_bit_7_cout),
    .Out1(Result[6]));  // open: Op, Sum
  ALU_1_bit alu_1_bit_8 (
    .A(A[7]), .B(B[7]), .B_Invert(Op[2]), .Cin(alu_1_bit_7_cout), .Less(1'b0), .Op(Op[1:0]),
    .Cout(alu_1_bit_8_cout), .Out1(Result[7]));  // open: Sum
  ALU_1_bit alu_1_bit_9 (
    .A(A[8]), .B(B[8]), .B_Invert(Op[2]), .Cin(alu_1_bit_8_cout), .Less(1'b0), .Op(Op[1:0]),
    .Cout(alu_1_bit_9_cout), .Out1(Result[8]));  // open: Sum
  ALU_1_bit alu_1_bit_10 (
    .A(A[9]), .B(B[9]), .B_Invert(Op[2]), .Cin(alu_1_bit_9_cout), .Less(1'b0), .Op(Op[1:0]),
    .Cout(alu_1_bit_10_cout), .Out1(Result[9]));  // open: Sum
  ALU_1_bit alu_1_bit_11 (
    .A(A[10]), .B(B[10]), .B_Invert(Op[2]), .Cin(alu_1_bit_10_cout), .Less(1'b0), .Op(Op[1:0]),
    .Cout(alu_1_bit_11_cout), .Out1(Result[10]));  // open: Sum
  ALU_1_bit alu_1_bit_12 (
    .A(A[11]), .B(B[11]), .B_Invert(Op[2]), .Cin(alu_1_bit_11_cout), .Less(1'b0), .Op(Op[1:0]),
    .Cout(alu_1_bit_12_cout), .Out1(Result[11]));  // open: Sum
  ALU_1_bit alu_1_bit_13 (
    .A(A[12]), .B(B[12]), .B_Invert(Op[2]), .Cin(alu_1_bit_12_cout), .Less(1'b0), .Op(Op[1:0]),
    .Cout(alu_1_bit_13_cout), .Out1(Result[12]));  // open: Sum
  ALU_1_bit alu_1_bit_14 (
    .A(A[13]), .B(B[13]), .B_Invert(Op[2]), .Cin(alu_1_bit_13_cout), .Less(1'b0), .Op(Op[1:0]),
    .Cout(alu_1_bit_14_cout), .Out1(Result[13]));  // open: Sum
  ALU_1_bit alu_1_bit_15 (
    .A(A[14]), .B(B[14]), .B_Invert(Op[2]), .Cin(alu_1_bit_14_cout), .Less(1'b0), .Op(Op[1:0]),
    .Cout(alu_1_bit_15_cout), .Out1(Result[14]));  // open: Sum
  ALU_1_bit alu_1_bit_16 (
    .A(A[15]), .B(B[15]), .B_Invert(Op[2]), .Cin(alu_1_bit_15_cout), .Less(1'b0), .Op(Op[1:0]),
    .Sum(alu_1_bit_16_sum), .Out1(Result[15]));  // open: Cout
  or or_1 (or_1_out, Result[0], Result[1], Result[2], Result[3], Result[4], Result[5], Result[6], Result[7], Result[8], Result[9], Result[10], Result[11], Result[12], Result[13], Result[14], Result[15]);
  not not_1 (Zero, or_1_out);
endmodule
