// Logisim project 11.2.circ as structural Verilog
module Controller (
  input  [3:0] opcode,
  input  [2:0] funct,
  output RegDst,
  output Branch,
  output RegWrite,
  output ALUSrc,
  output MemRead,
  output MemWrite,
  output MemtoReg,
  output [2:0] ALUOp
);
endmodule
